# Fritzing sketch RobotKit (saved by Fritzing 0.9.2b)
breadboards: 1

parts:
  Part1 = Arduino Uno (Rev3)
  Right_motor = DC Motor  # not connected
  Ultrasonic = SRF05 Ultrasonic Rangefinder
  Part3 = Motor Driver 1A Dual TB6612FNG  # not connected
  Mode_switch = Header 2 [package=r_sw_th]
  Power_switch = Header 2 [package=r_sw_th]
  Left_motor = DC Motor  # not connected
  VCC1 = 4 x AAA Battery Mount
  IC1 = Voltage Regulator [package=78xxl]
  J1 = Basic Servo
  IR_Receiver = TSOP312.., 314.. [package=THT]
  VCC2 = Battery block 9V  # not connected

nets:
  N1: Part1.D9_PWM, IR_Receiver.Data
  N2: Part1.D10_PWM/SS, J1.pulse
  GND: Part1.GND, Ultrasonic.GND, Mode_switch.1, VCC1.-, IC1.GND, J1.gnd, IR_Receiver.GND
  N3: Part1.D0/RX, Ultrasonic.Echo
  N4: Part1.D4, Mode_switch.2
  5V: Part1.5V, Ultrasonic.VCC, IR_Receiver.Vs
  N5: Power_switch.1, IC1.IN
  N6: Power_switch.2, VCC1.+
  N7: IC1.OUT, J1.vcc

custom parts:
  Motor Driver 1A Dual TB6612FNG: The TB6612FNG motor driver can control up to two DC motors at a constant current of 1.2A (3.2A peak). Two input signals (IN1 and IN2) can be used to control the motor in one of four function modes - CW, CCW, short-brake, and stop. The two motor outputs (A and B) can be separately controlled, the speed of each motor is controlled via a PWM input signal with a frequency up to 100kHz. The STBY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
